# Fritzing sketch Bluetooth basico (saved by Fritzing 0.9.3b)
breadboards: 1

parts:
  Part1 = Arduino Uno (Rev3)
  Part2 = Bluetooth HC-06
  KY-2 = Keyes Relay [package=THT]

nets:
  N1: Part1.D8, KY-2.signal
  N2: Part1.D0/RX, Part2.TXD
  N3: Part1.D1/TX, Part2.RXD
  5V: Part1.5V, Part2.VCC, KY-2.power
  GND: Part1.GND, Part2.GND, KY-2.ground

custom parts:
  Keyes Relay: The Keyes 5V relay module is suitable for SCM development, home appliance control. It uses a 5V~12V TIL control signal which can control DC / AC signal.
